// Logisim project VUDUCDUY_6651071008_bai1.circ as structural Verilog: 4 circuits, main circuit main
module main (
  input  A0,
  input  A1,
  input  A2,
  input  EN,
  output out_5,
  output out_6,
  output out_7,
  output out_8,
  output out_9,
  output out_10,
  output out_11,
  output out_12
);

  wire not_1_out, not_2_out, not_3_out, not_4_out, not_5_out, not_6_out, not_7_out, not_8_out, not_9_out,
       not_10_out, not_11_out, not_12_out;

  not not_1 (not_1_out, A0);
  not not_2 (not_2_out, A1);
  not not_3 (not_3_out, A0);
  not not_4 (not_4_out, A0);
  not not_5 (not_5_out, A0);
  not not_6 (not_6_out, A1);
  not not_7 (not_7_out, A0);
  not not_8 (not_8_out, A0);
  not not_9 (not_9_out, A1);
  not not_10 (not_10_out, A0);
  not not_11 (not_11_out, A0);
  not not_12 (not_12_out, A1);
  and and_1 (out_5, A0, A1, A0, A0);
  and and_2 (out_6, not_3_out, A1, A1, A0);
  and and_3 (out_7, A0, not_2_out, A0, A0);
  and and_4 (out_8, not_8_out, not_9_out, A0, A0);
  and and_5 (out_9, A0, A1, not_4_out, A0);
  and and_6 (out_10, not_10_out, A1, not_11_out, A0);
  and and_7 (out_11, A0, not_12_out, not_5_out, A0);
  and and_8 (out_12, not_1_out, not_6_out, not_7_out, A0);

  assign A2 = A0;
  assign EN = A0;
endmodule

module BAI2T1 (
  input  A,
  input  B,
  output AB,
  output A_OR_B,
  output notA,
  output A_XOR_B,
  output A_XNOR_B,
  output A_NAND_B,
  output A_NOR_B
);

  and and_1 (AB, A, B);
  or or_1 (A_OR_B, B, A);
  not not_1 (notA, A);
  nand nand_1 (A_NAND_B, A, B);
  nor nor_1 (A_NOR_B, A, B);
  xor xor_1 (A_XOR_B, B, A);
  xnor xnor_1 (A_XNOR_B, B, A);
endmodule

module D_latch (
  input  D3,
  input  D2,
  input  D1,
  input  D0,
  output Q3,
  output Q2,
  output Q1,
  output Q0
);

  wire clock_1_out;
  wire [3:0] register_1_q;

  Clock clock_1 (.out(clock_1_out));
  Register #(.width(4)) register_1 (.D({D3, D2, D1, D0}), .en(1'b1), .Q(register_1_q), .clk(clock_1_out), .clr(1'b0));
  Adder #(.width(4)) adder_1 (.a(4'b0010), .b(register_1_q), .out({Q3, Q2, Q1, Q0}));  // open: cin, cout
endmodule

module BAI1 (
  input  EN,
  input  A0,
  input  A1,
  input  A2,
  output Y0,
  output Y1,
  output Y2,
  output Y3,
  output Y4,
  output Y5,
  output Y6,
  output Y7
);

  wire not_1_out, not_2_out, not_3_out, not_4_out, not_5_out, not_6_out, not_7_out, not_8_out, not_9_out,
       not_10_out, not_11_out, not_12_out;

  not not_1 (not_1_out, A0);
  not not_2 (not_2_out, A1);
  not not_3 (not_3_out, A2);
  not not_4 (not_4_out, A0);
  not not_5 (not_5_out, A1);
  not not_6 (not_6_out, A0);
  not not_7 (not_7_out, A2);
  not not_8 (not_8_out, A0);
  not not_9 (not_9_out, A1);
  not not_10 (not_10_out, A2);
  not not_11 (not_11_out, A1);
  not not_12 (not_12_out, A2);
  and and_1 (Y7, EN, A0, A1, A2);
  and and_2 (Y0, EN, not_1_out, not_2_out, not_3_out);
  and and_3 (Y1, EN, not_4_out, not_5_out, A2);
  and and_4 (Y2, EN, not_6_out, A1, not_7_out);
  and and_5 (Y3, EN, not_8_out, A1, A2);
  and and_6 (Y4, EN, A0, not_9_out, not_10_out);
  and and_7 (Y5, EN, A0, not_11_out, A2);
  and and_8 (Y6, EN, A0, A1, not_12_out);
endmodule
