// Logisim project VUDUCDUY_6651071008_bai3.circ as structural Verilog: 1 circuit, main circuit main
module main (
  input  [3:0] A_3_0,
  input  [3:0] B_3_0,
  output [3:0] Sum_3_0,
  output Cout
);

  Adder #(.width(4)) adder_1 (.a(A_3_0), .b(B_3_0), .out(Sum_3_0), .cout(Cout));  // open: cin
endmodule
