// Logisim project VUDUCDUY_6651071008_bai4.circ as structural Verilog: 1 circuit, main circuit main
module main (
  input  [3:0] A_3_0,
  input  [3:0] B_3_0,
  output [3:0] Diff_3_0,
  output Borrow
);

  wire adder_1_p4;
  wire [3:0] not_1_out;

  assign not_1_out = ~B_3_0;  // NOT_Gate not_1, 4 bits wide
  // Adder #(.width(4)) adder_1: pin names not known; wires that end beside it: A_3_0, not_1_out, 1'b1, adder_1_p4, Diff_3_0
  not not_2 (Borrow, adder_1_p4);
endmodule
