// Logisim project VUDUCDUY_6651071008_bai5.circ as structural Verilog: 1 circuit, main circuit main
module main (
  input  [3:0] A_3_0,
  input  [3:0] B_3_0,
  output A___B,
  output A___B_2,
  output A___B_3
);

  Comparator #(.width(4)) comparator_1 (.a(A_3_0), .b(B_3_0), .eq(A___B_2));  // open: gt, lt
endmodule
