// Logisim project VUDUCDUY_6651071008_bai6.circ as structural Verilog: 1 circuit, main circuit main
module main (
  input  Reset,
  output [3:0] Q_3_0
);

  wire Clock_out, j_k_ff_1_q, j_k_ff_2_p3, j_k_ff_3_p1;

  Clock Clock (.out(Clock_out));
  J_K_Flip_Flop j_k_ff_1 (.K(Clock_out), .Q(j_k_ff_1_q), .Qn(Q_3_0[0]));  // open: J, clk, preset, en, reset
  // J_K_Flip_Flop j_k_ff_2: pin names not known; wires that end beside it: Reset, j_k_ff_1_q, j_k_ff_2_p3
  // J_K_Flip_Flop j_k_ff_3: pin names not known; wires that end beside it: j_k_ff_3_p1
  // J_K_Flip_Flop j_k_ff_4: pin names not known
endmodule
