// Logisim project VUDUCDUY_6651071008_bai7.circ as structural Verilog: 1 circuit, main circuit main
module main (
  input  [2:0] Addr_2_0,
  input  [3:0] Data_in_3_0,
  input  Load_Write,
  output [3:0] Data_out_3_0
);

  wire Clock_out;

  Clock Clock (.out(Clock_out));
  // RAM #(.addrWidth(3), .dataWidth(4), .bus("separate")) ram_1: pin names not known; wires that end beside it: Addr_2_0, Load_Write, Clock_out, Data_out_3_0
endmodule
